// Logisim project CPU.circ as structural Verilog: 33 circuits, main circuit ha
module dff (
  input  i,
  input  s,
  output o
);

  wire nand_1_out, nand_2_out, nand_4_out;

  nand nand_1 (nand_1_out, i, s);
  nand nand_2 (nand_2_out, nand_1_out, s);
  nand nand_3 (o, nand_1_out, nand_4_out);
  nand nand_4 (nand_4_out, o, nand_2_out);
endmodule

module ha (
  input  A,
  input  B,
  output S,
  output C
);

  xor xor_1 (S, A, B);
  and and_1 (C, A, B);
endmodule

module fa (
  input  Cpre,
  input  Ai,
  input  Bi,
  output Si,
  output Ci
);

  wire ha_1_c, ha_1_s, ha_2_c;

  ha ha_1 (.A(Ai), .B(Bi), .S(ha_1_s), .C(ha_1_c));
  ha ha_2 (.A(Cpre), .B(ha_1_s), .S(Si), .C(ha_2_c));
  or or_1 (Ci, ha_2_c, ha_1_c);

  // Notes on the sheet:
  //   繰り上がりのある 0 + 0
endmodule

module ADD (
  input  [3:0] a,
  input  [3:0] b,
  output [3:0] o,
  output CarryOut
);

  wire fa_1_ci, fa_2_ci, ha_1_c;

  ha ha_1 (.A(a[0]), .B(b[0]), .S(o[0]), .C(ha_1_c));
  fa fa_1 (.Cpre(ha_1_c), .Ai(a[1]), .Bi(b[1]), .Si(o[1]), .Ci(fa_1_ci));
  fa fa_2 (.Cpre(fa_1_ci), .Ai(a[2]), .Bi(b[2]), .Si(o[2]), .Ci(fa_2_ci));
  fa fa_3 (.Cpre(fa_2_ci), .Ai(a[3]), .Bi(b[3]), .Si(o[3]), .Ci(CarryOut));
endmodule

module DEC2 (
  input  in_1,
  input  in_2,
  output out_3,
  output out_4,
  output out_5,
  output out_6
);

  wire not_1_out, not_2_out, not_3_out, not_4_out;

  not not_1 (not_1_out, in_1);
  not not_2 (not_2_out, in_2);
  not not_3 (not_3_out, in_2);
  not not_4 (not_4_out, in_1);
  and and_1 (out_3, not_1_out, not_2_out);
  and and_2 (out_4, in_1, not_3_out);
  and and_3 (out_5, not_4_out, in_2);
  and and_4 (out_6, in_1, in_2);
endmodule

module DEC3 (
  input  [2:0] i,
  output out_2,
  output out_3,
  output out_4,
  output out_5,
  output out_6,
  output out_7,
  output out_8,
  output out_9
);

  wire not_1_out, not_2_out, not_3_out;

  not not_1 (not_1_out, i[0]);
  not not_2 (not_2_out, i[1]);
  not not_3 (not_3_out, i[2]);
  and and_1 (out_2, not_1_out, not_2_out, not_3_out);
  and and_2 (out_3, i[0], not_2_out, not_3_out);
  and and_3 (out_4, not_1_out, i[1], not_3_out);
  and and_4 (out_5, i[0], i[1], not_3_out);
  and and_5 (out_6, not_1_out, not_2_out, i[2]);
  and and_6 (out_7, i[0], not_2_out, i[2]);
  and and_7 (out_8, not_1_out, i[1], i[2]);
  and and_8 (out_9, i[0], i[1], i[2]);
endmodule

module DEC4 (
  input  [3:0] in_1,
  output out_2,
  output out_3,
  output out_4,
  output out_5,
  output out_6,
  output out_7,
  output out_8,
  output out_9,
  output out_10,
  output out_11,
  output out_12,
  output out_13,
  output out_14,
  output out_15,
  output out_16,
  output out_17
);

  wire not_1_out, not_2_out, not_3_out, not_4_out, not_5_out, not_6_out, not_7_out, not_8_out, not_9_out,
       not_10_out, not_11_out, not_12_out, not_13_out, not_14_out, not_15_out, not_16_out, not_17_out,
       not_18_out, not_19_out, not_20_out, not_21_out, not_22_out, not_23_out, not_24_out, not_25_out,
       not_26_out, not_27_out, not_28_out, not_29_out, not_30_out, not_31_out, not_32_out;

  not not_1 (not_1_out, in_1[0]);
  not not_2 (not_2_out, in_1[1]);
  not not_3 (not_3_out, in_1[2]);
  not not_4 (not_4_out, in_1[3]);
  not not_5 (not_5_out, in_1[1]);
  not not_6 (not_6_out, in_1[2]);
  not not_7 (not_7_out, in_1[3]);
  not not_8 (not_8_out, in_1[0]);
  not not_9 (not_9_out, in_1[2]);
  not not_10 (not_10_out, in_1[3]);
  not not_11 (not_11_out, in_1[2]);
  not not_12 (not_12_out, in_1[3]);
  not not_13 (not_13_out, in_1[0]);
  not not_14 (not_14_out, in_1[1]);
  not not_15 (not_15_out, in_1[3]);
  not not_16 (not_16_out, in_1[1]);
  not not_17 (not_17_out, in_1[3]);
  not not_18 (not_18_out, in_1[0]);
  not not_19 (not_19_out, in_1[3]);
  not not_20 (not_20_out, in_1[3]);
  not not_21 (not_21_out, in_1[0]);
  not not_22 (not_22_out, in_1[1]);
  not not_23 (not_23_out, in_1[2]);
  not not_24 (not_24_out, in_1[1]);
  not not_25 (not_25_out, in_1[2]);
  not not_26 (not_26_out, in_1[0]);
  not not_27 (not_27_out, in_1[2]);
  not not_28 (not_28_out, in_1[2]);
  not not_29 (not_29_out, in_1[0]);
  not not_30 (not_30_out, in_1[1]);
  not not_31 (not_31_out, in_1[1]);
  not not_32 (not_32_out, in_1[0]);
  and and_1 (out_2, not_1_out, not_2_out, not_3_out, not_4_out);
  and and_2 (out_3, in_1[0], not_5_out, not_6_out, not_7_out);
  and and_3 (out_4, not_8_out, in_1[1], not_9_out, not_10_out);
  and and_4 (out_5, in_1[0], in_1[1], not_11_out, not_12_out);
  and and_5 (out_6, not_13_out, not_14_out, in_1[2], not_15_out);
  and and_6 (out_7, in_1[0], not_16_out, in_1[2], not_17_out);
  and and_7 (out_8, not_18_out, in_1[1], in_1[2], not_19_out);
  and and_8 (out_9, in_1[0], in_1[1], in_1[2], not_20_out);
  and and_9 (out_10, not_21_out, not_22_out, not_23_out, in_1[3]);
  and and_10 (out_11, in_1[0], not_24_out, not_25_out, in_1[3]);
  and and_11 (out_12, not_26_out, in_1[1], not_27_out, in_1[3]);
  and and_12 (out_13, in_1[0], in_1[1], not_28_out, in_1[3]);
  and and_13 (out_14, not_29_out, not_30_out, in_1[2], in_1[3]);
  and and_14 (out_15, in_1[0], not_31_out, in_1[2], in_1[3]);
  and and_15 (out_16, not_32_out, in_1[1], in_1[2], in_1[3]);
  and and_16 (out_17, in_1[0], in_1[1], in_1[2], in_1[3]);
endmodule

module DEC (
  input  in_1,
  input  in_2,
  output o00,
  output o01,
  output o10,
  output o11
);

  DEC2 dec2_1 (.in_1(in_1), .in_2(in_2), .out_3(o00), .out_4(o01), .out_5(o10), .out_6(o11));
endmodule

module RAM4 (
  input  in_1,
  input  in_2,
  input  in_3,
  input  in_4,
  input  in_5,
  input  in_6,
  input  in_7,
  input  in_8
);

  wire dec4_1_p6, dec4_1_p7, dec4_1_p8, dec4_1_p9, dec4_1_p10, dec4_1_p11, dec4_1_p12, dec4_1_p13,
       dec4_1_p14, dec4_1_p15, dec4_1_p16, dec4_1_p17, dec4_1_p18, dec4_1_p19, dec4_1_p20, dec4_1_p21,
       dec4_1_p22, dec4_1_p23, dec4_2_p3, dec4_2_p4, dec4_2_p5, dec4_2_p6, dec4_2_p8, dec4_2_p10, dec4_2_p12,
       dec4_2_p14, dec4_2_p15, dec4_2_p16, dec4_2_p17, dec4_2_p18, dec4_2_p19, dec4_2_p20;

  // DEC4 dec4_1: pin names not known; wires that end beside it: in_4, in_5, in_6, in_7, in_8, dec4_1_p6, dec4_1_p7, dec4_1_p8, dec4_1_p9, dec4_1_p10, dec4_1_p11, dec4_1_p12, dec4_1_p13, dec4_1_p14, dec4_1_p15, dec4_1_p16, dec4_1_p17, dec4_1_p18, dec4_1_p19, dec4_1_p20, dec4_1_p21, dec4_1_p22, dec4_1_p23
  // DEC4 dec4_2: pin names not known; wires that end beside it: dec4_1_p22, dec4_1_p23, dec4_2_p3, dec4_2_p4, dec4_2_p5, dec4_2_p6, in_4, dec4_2_p8, in_3, dec4_2_p10, in_2, dec4_2_p12, in_1, dec4_2_p14, dec4_2_p15, dec4_2_p16, dec4_2_p17, dec4_2_p18, dec4_2_p19, dec4_2_p20, dec4_1_p6, dec4_1_p7, dec4_1_p8
endmodule

module Z (
  input  [7:0] i,
  output zero
);

  wire or_1_out;

  or or_1 (or_1_out, i[0], i[1], i[2], i[3], i[4], i[5], i[6], i[7]);
  not not_1 (zero, or_1_out);
endmodule

module En (
  input  [7:0] i,
  input  e,
  output [7:0] o
);

  and and_1 (o[0], i[0], e);
  and and_2 (o[1], i[1], e);
  and and_3 (o[2], i[2], e);
  and and_4 (o[3], i[3], e);
  and and_5 (o[4], i[4], e);
  and and_6 (o[5], i[5], e);
  and and_7 (o[6], i[6], e);
  and and_8 (o[7], i[7], e);
endmodule

module m (
  input  i,
  input  s,
  output o
);

  D_Flip_Flop d_ff_1 (.D(i), .clk(s), .Q(o));  // open: Qn, preset, reset
endmodule

module Stp (
  input  reset,
  input  clk,
  output stp1,
  output stp2,
  output stp3,
  output stp4,
  output stp5,
  output stp6,
  output stp7
);

  wire m_1_o, m_2_o, m_3_o, m_4_o, m_5_o, m_6_o, m_7_o, m_8_o, m_9_o, m_10_o, m_11_o, not_1_out, not_2_out,
       not_3_out, not_4_out, not_5_out, not_6_out, not_7_out, not_8_out, or_1_out, or_2_out;

  not not_1 (not_1_out, clk);
  not not_2 (not_2_out, reset);
  or or_1 (or_1_out, reset, not_1_out);
  or or_2 (or_2_out, reset, clk);
  m m_1 (.i(not_2_out), .s(or_1_out), .o(m_1_o));
  or or_3 (stp1, reset, not_3_out);
  not not_3 (not_3_out, m_2_o);
  m m_2 (.i(m_1_o), .s(or_2_out), .o(m_2_o));
  m m_3 (.i(m_2_o), .s(or_1_out), .o(m_3_o));
  and and_1 (stp2, m_2_o, not_4_out);
  not not_4 (not_4_out, m_4_o);
  m m_4 (.i(m_3_o), .s(or_2_out), .o(m_4_o));
  m m_5 (.i(m_4_o), .s(or_1_out), .o(m_5_o));
  and and_2 (stp3, m_4_o, not_5_out);
  not not_5 (not_5_out, m_6_o);
  m m_6 (.i(m_5_o), .s(or_2_out), .o(m_6_o));
  m m_7 (.i(m_6_o), .s(or_1_out), .o(m_7_o));
  and and_3 (stp4, m_6_o, not_6_out);
  not not_6 (not_6_out, m_8_o);
  m m_8 (.i(m_7_o), .s(or_2_out), .o(m_8_o));
  m m_9 (.i(m_8_o), .s(or_1_out), .o(m_9_o));
  and and_4 (stp5, m_8_o, not_7_out);
  not not_7 (not_7_out, m_10_o);
  m m_10 (.i(m_9_o), .s(or_2_out), .o(m_10_o));
  m m_11 (.i(m_10_o), .s(or_1_out), .o(m_11_o));
  and and_5 (stp6, m_10_o, not_8_out);
  not not_8 (not_8_out, stp7);
  m m_12 (.i(m_11_o), .s(or_2_out), .o(stp7));
endmodule

module AD (
  input  carryin,
  input  [7:0] a,
  input  [7:0] b,
  output [7:0] o,
  output carryout
);

  wire fa_1_ci, fa_2_ci, fa_3_ci, fa_4_ci, fa_5_ci, fa_6_ci, fa_7_ci;

  fa fa_1 (.Cpre(carryin), .Ai(a[0]), .Bi(b[0]), .Si(o[0]), .Ci(fa_1_ci));
  fa fa_2 (.Cpre(fa_1_ci), .Ai(a[1]), .Bi(b[1]), .Si(o[1]), .Ci(fa_2_ci));
  fa fa_3 (.Cpre(fa_2_ci), .Ai(a[2]), .Bi(b[2]), .Si(o[2]), .Ci(fa_3_ci));
  fa fa_4 (.Cpre(fa_3_ci), .Ai(a[3]), .Bi(b[3]), .Si(o[3]), .Ci(fa_4_ci));
  fa fa_5 (.Cpre(fa_4_ci), .Ai(a[4]), .Bi(b[4]), .Si(o[4]), .Ci(fa_5_ci));
  fa fa_6 (.Cpre(fa_5_ci), .Ai(a[5]), .Bi(b[5]), .Si(o[5]), .Ci(fa_6_ci));
  fa fa_7 (.Cpre(fa_6_ci), .Ai(a[6]), .Bi(b[6]), .Si(o[6]), .Ci(fa_7_ci));
  fa fa_8 (.Cpre(fa_7_ci), .Ai(a[7]), .Bi(b[7]), .Si(o[7]), .Ci(carryout));
endmodule

module SHL (
  input  [7:0] i,
  input  shiftin,
  output shiftout,
  output [7:0] o
);


  assign o = {shiftin, i[7:1]};
  assign shiftout = i[0];
endmodule

module SHR (
  input  shiftin,
  input  [7:0] i,
  output [7:0] o,
  output shiftout
);


  assign o = {i[6:0], shiftin};
  assign shiftout = i[7];
endmodule

module comp (
  input  alleq,
  input  alargerI,
  input  a,
  input  b,
  output c,
  output alleqsofar,
  output alargerO
);

  wire and_2_out, not_1_out;

  xor xor_1 (c, a, b);
  not not_1 (not_1_out, c);
  and and_1 (alleqsofar, not_1_out, alleq);
  and and_2 (and_2_out, alleq, a, c);
  or or_1 (alargerO, and_2_out, alargerI);
endmodule

module COM (
  input  [7:0] a,
  input  [7:0] b,
  output [7:0] XORo,
  output equal,
  output alarger
);

  wire comp_1_alargero, comp_1_alleqsofar, comp_2_alargero, comp_2_alleqsofar, comp_3_alargero,
       comp_3_alleqsofar, comp_4_alargero, comp_4_alleqsofar, comp_5_alargero, comp_5_alleqsofar,
       comp_6_alargero, comp_6_alleqsofar, comp_7_alargero, comp_7_alleqsofar;

  comp comp_1 (
    .alleq(1'b1), .a(a[0]), .b(b[0]), .c(XORo[0]), .alleqsofar(comp_1_alleqsofar), .alargerO(comp_1_alargero));  // open: alargerI
  comp comp_2 (
    .alleq(comp_1_alleqsofar), .alargerI(comp_1_alargero), .a(a[1]), .b(b[1]), .c(XORo[1]),
    .alleqsofar(comp_2_alleqsofar), .alargerO(comp_2_alargero));
  comp comp_3 (
    .alleq(comp_2_alleqsofar), .alargerI(comp_2_alargero), .a(a[2]), .b(b[2]), .c(XORo[2]),
    .alleqsofar(comp_3_alleqsofar), .alargerO(comp_3_alargero));
  comp comp_4 (
    .alleq(comp_3_alleqsofar), .alargerI(comp_3_alargero), .a(a[3]), .b(b[3]), .c(XORo[3]),
    .alleqsofar(comp_4_alleqsofar), .alargerO(comp_4_alargero));
  comp comp_5 (
    .alleq(comp_4_alleqsofar), .alargerI(comp_4_alargero), .a(a[4]), .b(b[4]), .c(XORo[4]),
    .alleqsofar(comp_5_alleqsofar), .alargerO(comp_5_alargero));
  comp comp_6 (
    .alleq(comp_5_alleqsofar), .alargerI(comp_5_alargero), .a(a[5]), .b(b[5]), .c(XORo[5]),
    .alleqsofar(comp_6_alleqsofar), .alargerO(comp_6_alargero));
  comp comp_7 (
    .alleq(comp_6_alleqsofar), .alargerI(comp_6_alargero), .a(a[6]), .b(b[6]), .c(XORo[6]),
    .alleqsofar(comp_7_alleqsofar), .alargerO(comp_7_alargero));
  comp comp_8 (
    .alleq(comp_7_alleqsofar), .alargerI(comp_7_alargero), .a(a[7]), .b(b[7]), .c(XORo[7]),
    .alleqsofar(equal), .alargerO(alarger));
endmodule

module ALU (
  input  [7:0] a,
  input  [7:0] b,
  input  carrryin,
  input  [2:0] op,
  output [7:0] c,
  output equal,
  output alarge,
  output carryout,
  output zero
);

  wire ad_1_carryout, and_2_out, and_3_out, and_4_out, dec3_1_out_2, dec3_1_out_3, dec3_1_out_4,
       dec3_1_out_5, dec3_1_out_6, dec3_1_out_7, dec3_1_out_8, shl_1_shiftout, shr_1_shiftout;
  wire [7:0] ad_1_o, and_1_out, com_1_xoro, en_1_o, en_2_o, en_3_o, en_4_o, en_5_o, en_6_o, en_7_o,
       not_1_out, or_1_out, shl_1_o, shr_1_o;

  assign or_1_out = a | b;  // OR_Gate or_1, 8 bits wide
  assign and_1_out = a & b;  // AND_Gate and_1, 8 bits wide
  assign not_1_out = ~a;  // NOT_Gate not_1, 8 bits wide
  COM com_1 (.a(a), .b(b), .XORo(com_1_xoro), .equal(equal), .alarger(alarge));
  SHL shl_1 (.i(a), .shiftin(carrryin), .shiftout(shl_1_shiftout), .o(shl_1_o));
  SHR shr_1 (.shiftin(carrryin), .i(a), .o(shr_1_o), .shiftout(shr_1_shiftout));
  AD ad_1 (.carryin(carrryin), .a(a), .b(b), .o(ad_1_o), .carryout(ad_1_carryout));
  DEC3 dec3_1 (
    .i(op), .out_2(dec3_1_out_2), .out_3(dec3_1_out_3), .out_4(dec3_1_out_4), .out_5(dec3_1_out_5),
    .out_6(dec3_1_out_6), .out_7(dec3_1_out_7), .out_8(dec3_1_out_8));  // open: out_9
  En en_1 (.i(com_1_xoro), .e(dec3_1_out_8), .o(en_1_o));
  En en_2 (.i(or_1_out), .e(dec3_1_out_7), .o(en_2_o));
  En en_3 (.i(and_1_out), .e(dec3_1_out_6), .o(en_3_o));
  En en_4 (.i(not_1_out), .e(dec3_1_out_5), .o(en_4_o));
  En en_5 (.i(shl_1_o), .e(dec3_1_out_4), .o(en_5_o));
  En en_6 (.i(shr_1_o), .e(dec3_1_out_3), .o(en_6_o));
  En en_7 (.i(ad_1_o), .e(dec3_1_out_2), .o(en_7_o));
  and and_2 (and_2_out, shl_1_shiftout, dec3_1_out_4);
  and and_3 (and_3_out, shr_1_shiftout, dec3_1_out_3);
  and and_4 (and_4_out, ad_1_carryout, dec3_1_out_2);
  assign c = en_1_o | en_2_o | en_3_o | en_4_o | en_5_o | en_6_o | en_7_o;  // OR_Gate or_2, 8 bits wide
  or or_3 (carryout, and_2_out, and_3_out, and_4_out);
  Z z_1 (.i(en_7_o), .zero(zero));
endmodule

module R (
  input  [7:0] i,
  input  s,
  input  e,
  output [7:0] o,
  output [7:0] display
);

  m m_1 (.i(i[0]), .s(s), .o(display[0]));
  m m_2 (.i(i[1]), .s(s), .o(display[1]));
  m m_3 (.i(i[2]), .s(s), .o(display[2]));
  m m_4 (.i(i[3]), .s(s), .o(display[3]));
  m m_5 (.i(i[4]), .s(s), .o(display[4]));
  m m_6 (.i(i[5]), .s(s), .o(display[5]));
  m m_7 (.i(i[6]), .s(s), .o(display[6]));
  m m_8 (.i(i[7]), .s(s), .o(display[7]));
  and and_1 (o[0], display[0], e);
  and and_2 (o[1], display[1], e);
  and and_3 (o[2], display[2], e);
  and and_4 (o[3], display[3], e);
  and and_5 (o[4], display[4], e);
  and and_6 (o[5], display[5], e);
  and and_7 (o[6], display[6], e);
  and and_8 (o[7], display[7], e);
endmodule

module bus1 (
  input  [7:0] i,
  input  one,
  output [7:0] o
);

  wire not_1_out;

  not not_1 (not_1_out, one);
  or or_1 (o[0], i[0], one);
  and and_1 (o[1], i[1], not_1_out);
  and and_2 (o[2], i[2], not_1_out);
  and and_3 (o[3], i[3], not_1_out);
  and and_4 (o[4], i[4], not_1_out);
  and and_5 (o[5], i[5], not_1_out);
  and and_6 (o[6], i[6], not_1_out);
  and and_7 (o[7], i[7], not_1_out);
endmodule

module IR (
  input  [7:0] i,
  input  s,
  output o0,
  output o1,
  output o2,
  output o3,
  output o4,
  output o5,
  output o6,
  output o7,
  output out_11
);

  m m_1 (.i(i[0]), .s(s), .o(o7));
  m m_2 (.i(i[1]), .s(s), .o(o6));
  m m_3 (.i(i[2]), .s(s), .o(o5));
  m m_4 (.i(i[3]), .s(s), .o(o4));
  m m_5 (.i(i[4]), .s(s), .o(o3));
  m m_6 (.i(i[5]), .s(s), .o(o2));
  m m_7 (.i(i[6]), .s(s), .o(o1));
  m m_8 (.i(i[7]), .s(s), .o(o0));
endmodule

module TMP (
  input  [7:0] i,
  input  s,
  output [7:0] o
);

  m m_1 (.i(i[0]), .s(s), .o(o[0]));
  m m_2 (.i(i[1]), .s(s), .o(o[1]));
  m m_3 (.i(i[2]), .s(s), .o(o[2]));
  m m_4 (.i(i[3]), .s(s), .o(o[3]));
  m m_5 (.i(i[4]), .s(s), .o(o[4]));
  m m_6 (.i(i[5]), .s(s), .o(o[5]));
  m m_7 (.i(i[6]), .s(s), .o(o[6]));
  m m_8 (.i(i[7]), .s(s), .o(o[7]));
endmodule

module FlagsR (
  input  iC,
  input  iA,
  input  iE,
  input  iZ,
  input  s,
  output oC,
  output oA,
  output oE,
  output oZ
);

  m m_1 (.i(iC), .s(s), .o(oC));
  m m_2 (.i(iA), .s(s), .o(oA));
  m m_3 (.i(iE), .s(s), .o(oE));
  m m_4 (.i(iZ), .s(s), .o(oZ));
endmodule

module MAR (
  input  [7:0] i,
  input  s,
  output [7:0] o
);

  m m_1 (.i(i[0]), .s(s), .o(o[0]));
  m m_2 (.i(i[1]), .s(s), .o(o[1]));
  m m_3 (.i(i[2]), .s(s), .o(o[2]));
  m m_4 (.i(i[3]), .s(s), .o(o[3]));
  m m_5 (.i(i[4]), .s(s), .o(o[4]));
  m m_6 (.i(i[5]), .s(s), .o(o[5]));
  m m_7 (.i(i[6]), .s(s), .o(o[6]));
  m m_8 (.i(i[7]), .s(s), .o(o[7]));
endmodule

module Controller (
  input  reseter,
  input  clk,
  input  carryout,
  input  alarger,
  input  equal,
  input  zero,
  input  i0,
  input  i1,
  input  i2,
  input  i3,
  input  i4,
  input  i5,
  input  i6,
  input  i7,
  output sIR,
  output bus1,
  output sMAR,
  output eIAR,
  output sIAR,
  output eRAM,
  output sACC,
  output eACC,
  output sRAM,
  output eclk,
  output sTMP,
  output sFlag,
  output sclk,
  output sR0,
  output eR0,
  output sR1,
  output eR1,
  output sR2,
  output eR2,
  output sR3,
  output eR3,
  output dataadress,
  output inputoutput,
  output [2:0] toALU
);

  wire A_out, and_5_out, and_6_out, and_7_out, and_8_out, and_9_out, and_10_out, and_11_out, and_12_out,
       and_16_out, and_17_out, and_18_out, and_19_out, and_20_out, and_21_out, and_22_out, and_23_out,
       and_24_out, and_25_out, and_26_out, and_27_out, and_28_out, and_29_out, and_30_out, and_31_out,
       and_32_out, and_33_out, and_34_out, and_35_out, and_36_out, and_37_out, and_38_out, and_39_out,
       and_40_out, and_41_out, and_42_out, and_43_out, C_out, dec2_1_out_3, dec2_1_out_4, dec2_1_out_5,
       dec2_1_out_6, dec2_2_out_3, dec2_2_out_4, dec2_2_out_5, dec2_2_out_6, dec2_3_out_3, dec2_3_out_4,
       dec2_3_out_5, dec2_3_out_6, dec3_1_out_2, dec3_1_out_3, dec3_1_out_4, dec3_1_out_5, dec3_1_out_6,
       dec3_1_out_7, dec3_1_out_8, dec3_1_out_9, E_out, eA_out, eB_out, not_1_out, not_2_out, not_3_out,
       or_6_out, or_7_out, or_8_out, or_9_out, or_10_out, or_11_out, or_12_out, or_13_out, sB_out,
       stp_1_stp1, stp_1_stp2, stp_1_stp3, stp_1_stp4, stp_1_stp5, stp_1_stp6, stp_1_stp7, Z_out;

  or or_1 (eR0, and_5_out, and_9_out);
  or or_2 (eR1, and_6_out, and_10_out);
  or or_3 (eR2, and_7_out, and_11_out);
  or or_4 (eR3, and_8_out, and_12_out);
  or or_5 (bus1, stp_1_stp1, and_27_out, and_30_out, and_31_out);
  and and_1 (eIAR, clk, or_6_out);
  or or_6 (or_6_out, stp_1_stp1, and_27_out, and_29_out, and_30_out);
  and and_2 (eRAM, clk, or_7_out);
  or or_7 (or_7_out, stp_1_stp2, and_34_out, and_36_out, and_37_out, and_43_out);
  and and_3 (eACC, clk, or_8_out);
  or or_8 (or_8_out, stp_1_stp3, and_41_out, and_42_out, and_38_out);
  and and_4 (eclk, clk, and_39_out);
  and and_5 (and_5_out, clk, eB_out, dec2_1_out_3);
  and and_6 (and_6_out, clk, eB_out, dec2_1_out_4);
  and and_7 (and_7_out, clk, eB_out, dec2_1_out_5);
  and and_8 (and_8_out, clk, eB_out, dec2_1_out_6);
  and and_9 (and_9_out, clk, eA_out, dec2_2_out_3);
  and and_10 (and_10_out, clk, eA_out, dec2_2_out_4);
  and and_11 (and_11_out, clk, eA_out, dec2_2_out_5);
  and and_12 (and_12_out, clk, eA_out, dec2_2_out_6);
  or eB (eB_out, and_24_out, and_35_out, and_28_out, and_32_out);
  or eA (eA_out, and_33_out, and_25_out, and_26_out);
  or or_9 (or_9_out, reseter, stp_1_stp7);
  not not_1 (not_1_out, i0);
  Stp stp_1 (
    .reset(or_9_out), .clk(clk), .stp1(stp_1_stp1), .stp2(stp_1_stp2), .stp3(stp_1_stp3), .stp4(stp_1_stp4),
    .stp5(stp_1_stp5), .stp6(stp_1_stp6), .stp7(stp_1_stp7));
  DEC3 dec3_1 (
    .i({i1, i2, i3}), .out_2(dec3_1_out_2), .out_3(dec3_1_out_3), .out_4(dec3_1_out_4), .out_5(dec3_1_out_5),
    .out_6(dec3_1_out_6), .out_7(dec3_1_out_7), .out_8(dec3_1_out_8), .out_9(dec3_1_out_9));
  and and_13 (toALU[0], stp_1_stp5, i0, i3);
  and and_14 (toALU[1], stp_1_stp5, i0, i2);
  and and_15 (toALU[2], stp_1_stp5, i0, i1);
  and and_16 (and_16_out, not_1_out, dec3_1_out_2);
  and and_17 (and_17_out, not_1_out, dec3_1_out_3);
  and and_18 (and_18_out, not_1_out, dec3_1_out_4);
  and and_19 (and_19_out, not_1_out, dec3_1_out_5);
  and and_20 (and_20_out, not_1_out, dec3_1_out_6);
  and and_21 (and_21_out, not_1_out, dec3_1_out_7);
  and and_22 (and_22_out, not_1_out, dec3_1_out_8);
  and and_23 (and_23_out, not_1_out, dec3_1_out_9);
  DEC2 dec2_1 (
    .in_1(i7), .in_2(i6), .out_3(dec2_1_out_3), .out_4(dec2_1_out_4), .out_5(dec2_1_out_5),
    .out_6(dec2_1_out_6));
  DEC2 dec2_2 (
    .in_1(i5), .in_2(i4), .out_3(dec2_2_out_3), .out_4(dec2_2_out_4), .out_5(dec2_2_out_5),
    .out_6(dec2_2_out_6));
  and and_24 (and_24_out, stp_1_stp4, i0);
  and and_25 (and_25_out, stp_1_stp4, and_16_out);
  and and_26 (and_26_out, stp_1_stp4, and_17_out);
  and and_27 (and_27_out, stp_1_stp4, and_18_out);
  and and_28 (and_28_out, stp_1_stp4, and_19_out);
  and and_29 (and_29_out, stp_1_stp4, and_20_out);
  and and_30 (and_30_out, stp_1_stp4, and_21_out);
  and and_31 (and_31_out, stp_1_stp4, and_22_out);
  and and_32 (and_32_out, stp_1_stp4, and_23_out, i4);
  not not_2 (not_2_out, i4);
  and and_33 (and_33_out, stp_1_stp5, i0);
  and and_34 (and_34_out, stp_1_stp5, and_16_out);
  and and_35 (and_35_out, stp_1_stp5, and_17_out);
  and and_36 (and_36_out, stp_1_stp5, and_18_out);
  and and_37 (and_37_out, stp_1_stp5, and_20_out);
  and and_38 (and_38_out, stp_1_stp5, and_21_out);
  and and_39 (and_39_out, stp_1_stp5, and_23_out, not_2_out);
  and C (C_out, carryout, i4);
  and A (A_out, alarger, i5);
  and E (E_out, equal, i6);
  and Z (Z_out, zero, i7);
  and and_40 (and_40_out, i3, i2, i1);
  or or_10 (or_10_out, C_out, A_out, E_out, Z_out);
  not not_3 (not_3_out, and_40_out);
  and and_41 (and_41_out, stp_1_stp6, not_3_out, i0);
  and and_42 (and_42_out, stp_1_stp6, and_18_out);
  and and_43 (and_43_out, stp_1_stp6, or_10_out, and_21_out);
  DEC2 dec2_3 (
    .in_1(i7), .in_2(i6), .out_3(dec2_3_out_3), .out_4(dec2_3_out_4), .out_5(dec2_3_out_5),
    .out_6(dec2_3_out_6));
  or sB (sB_out, and_41_out, and_34_out, and_36_out, and_39_out);
  and and_44 (sIR, clk, stp_1_stp2);
  and and_45 (sMAR, clk, or_11_out);
  or or_11 (or_11_out, stp_1_stp1, and_25_out, and_26_out, and_27_out, and_29_out, and_30_out);
  and and_46 (sIAR, clk, or_12_out);
  or or_12 (or_12_out, stp_1_stp3, and_42_out, and_28_out, and_37_out, and_38_out, and_43_out);
  and and_47 (sACC, clk, or_13_out);
  or or_13 (or_13_out, stp_1_stp1, and_33_out, and_27_out, and_30_out);
  and and_48 (sRAM, clk, and_35_out);
  and and_49 (sTMP, clk, and_24_out);
  and and_50 (sFlag, clk, and_31_out);
  and and_51 (sclk, clk, and_32_out);
  and and_52 (sR0, clk, sB_out, dec2_3_out_3);
  and and_53 (sR1, clk, sB_out, dec2_3_out_4);
  and and_54 (sR2, clk, sB_out, dec2_3_out_5);
  and and_55 (sR3, clk, sB_out, dec2_3_out_6);

  assign dataadress = i5;
  assign inputoutput = i4;
endmodule

module CPU (
  input  iniset,
  input  reset,
  input  clk
);

  wire alu_1_alarge, alu_1_carryout, alu_1_equal, alu_1_zero, controller_1_bus1, controller_1_dataadress,
       controller_1_eacc, controller_1_eclk, controller_1_eiar, controller_1_er0, controller_1_er1,
       controller_1_er2, controller_1_er3, controller_1_eram, controller_1_inputoutput, controller_1_sacc,
       controller_1_sclk, controller_1_sflag, controller_1_siar, controller_1_sir, controller_1_smar,
       controller_1_sr0, controller_1_sr1, controller_1_sr2, controller_1_sr3, controller_1_sram,
       controller_1_stmp, flagsr_1_oa, flagsr_1_oc, flagsr_1_oe, flagsr_1_oz, ir_1_o0, ir_1_o1, ir_1_o2,
       ir_1_o3, ir_1_o4, ir_1_o5, ir_1_o6, ir_1_o7, or_1_out, or_2_out;
  wire [2:0] controller_1_toalu;
  wire [7:0] ACC_o, alu_1_c, bus1_1_o, mar_1_o, or_3_out, R0_o, ram_1_dout, tmp_1_o;

  IR ir_1 (
    .i(R0_o), .s(controller_1_sir), .o0(ir_1_o0), .o1(ir_1_o1), .o2(ir_1_o2), .o3(ir_1_o3), .o4(ir_1_o4),
    .o5(ir_1_o5), .o6(ir_1_o6), .o7(ir_1_o7));  // open: out_11
  TMP tmp_1 (.i(R0_o), .s(controller_1_stmp), .o(tmp_1_o));
  FlagsR flagsr_1 (
    .iC(alu_1_carryout), .iA(alu_1_alarge), .iE(alu_1_equal), .iZ(alu_1_zero), .s(controller_1_sflag),
    .oC(flagsr_1_oc), .oA(flagsr_1_oa), .oE(flagsr_1_oe), .oZ(flagsr_1_oz));
  bus1 bus1_1 (.i(tmp_1_o), .one(controller_1_bus1), .o(bus1_1_o));
  Controller controller_1 (
    .reseter(reset), .clk(clk), .carryout(flagsr_1_oc), .alarger(flagsr_1_oa), .equal(flagsr_1_oe),
    .zero(flagsr_1_oz), .i0(ir_1_o0), .i1(ir_1_o1), .i2(ir_1_o2), .i3(ir_1_o3), .i4(ir_1_o4), .i5(ir_1_o5),
    .i6(ir_1_o6), .i7(ir_1_o7), .sIR(controller_1_sir), .bus1(controller_1_bus1), .sMAR(controller_1_smar),
    .eIAR(controller_1_eiar), .sIAR(controller_1_siar), .eRAM(controller_1_eram), .sACC(controller_1_sacc),
    .eACC(controller_1_eacc), .sRAM(controller_1_sram), .eclk(controller_1_eclk), .sTMP(controller_1_stmp),
    .sFlag(controller_1_sflag), .sclk(controller_1_sclk), .sR0(controller_1_sr0), .eR0(controller_1_er0),
    .sR1(controller_1_sr1), .eR1(controller_1_er1), .sR2(controller_1_sr2), .eR2(controller_1_er2),
    .sR3(controller_1_sr3), .eR3(controller_1_er3), .dataadress(controller_1_dataadress),
    .inputoutput(controller_1_inputoutput), .toALU(controller_1_toalu));
  ALU alu_1 (
    .a(R0_o), .b(bus1_1_o), .carrryin(flagsr_1_oc), .op(controller_1_toalu), .c(alu_1_c),
    .equal(alu_1_equal), .alarge(alu_1_alarge), .carryout(alu_1_carryout), .zero(alu_1_zero));
  R ACC (.i(alu_1_c), .s(controller_1_sacc), .e(controller_1_eacc), .o(ACC_o));  // open: display
  or or_1 (or_1_out, controller_1_eram, iniset);
  MAR mar_1 (.i(R0_o), .s(controller_1_smar), .o(mar_1_o));
  or or_2 (or_2_out, clk, iniset);
  RAM ram_1 (.addr(mar_1_o), .we(controller_1_sram), .oe(or_1_out), .clk(or_2_out), .din(ACC_o), .dout(ram_1_dout));
  assign or_3_out = ram_1_dout | ACC_o;  // OR_Gate or_3, 8 bits wide
  R R0 (.i(or_3_out), .s(controller_1_sr0), .e(controller_1_er0), .o(R0_o));  // open: display
  R R1 (.i(or_3_out), .s(controller_1_sr1), .e(controller_1_er1), .o(R0_o));  // open: display
  R R2 (.i(or_3_out), .s(controller_1_sr2), .e(controller_1_er2), .o(R0_o));  // open: display
  R R3 (.i(or_3_out), .s(controller_1_sr3), .e(controller_1_er3), .o(R0_o));  // open: display
  R IAR (.i(or_3_out), .s(controller_1_siar), .e(controller_1_eiar), .o(R0_o));  // open: display
endmodule

module Demo (
  input  in_1,
  input  in_2,
  input  OR,
  input  in_4,
  input  XOR,
  input  in_6,
  input  NOT
);

  wire and_1_out, not_1_out, or_1_out, xor_1_out;

  and and_1 (and_1_out, in_1, in_2);
  not not_1 (not_1_out, NOT);
  LED led_1 (.in(and_1_out));
  or or_1 (or_1_out, OR, in_4);
  LED led_2 (.in(or_1_out));
  xor xor_1 (xor_1_out, XOR, in_6);
  LED led_3 (.in(xor_1_out));
  LED led_4 (.in(not_1_out));

  // Notes on the sheet:
  //   AND
endmodule

module RegisterDemo (
  input  [7:0] i,
  input  s,
  input  e,
  output [7:0] o
);

  wire m_1_o, m_2_o, m_3_o, m_4_o, m_5_o, m_6_o, m_7_o, m_8_o;

  m m_1 (.i(i[0]), .s(s), .o(m_1_o));
  m m_2 (.i(i[1]), .s(s), .o(m_2_o));
  m m_3 (.i(i[2]), .s(s), .o(m_3_o));
  m m_4 (.i(i[3]), .s(s), .o(m_4_o));
  m m_5 (.i(i[4]), .s(s), .o(m_5_o));
  m m_6 (.i(i[5]), .s(s), .o(m_6_o));
  m m_7 (.i(i[6]), .s(s), .o(m_7_o));
  m m_8 (.i(i[7]), .s(s), .o(m_8_o));
  and and_1 (o[0], m_1_o, e);
  and and_2 (o[1], m_2_o, e);
  and and_3 (o[2], m_3_o, e);
  and and_4 (o[3], m_4_o, e);
  and and_5 (o[4], m_5_o, e);
  and and_6 (o[5], m_6_o, e);
  and and_7 (o[6], m_7_o, e);
  and and_8 (o[7], m_8_o, e);
endmodule

module MemoryDemo (
  input  InputMemory,
  input  SetMemory,
  output memory
);

  dff dff_1 (.i(InputMemory), .s(SetMemory), .o(memory));
endmodule

module RamAddressDemo (
  input  [7:0] address
);

  wire dec4_1_out_2, dec4_1_out_3, dec4_1_out_4, dec4_1_out_5, dec4_1_out_6, dec4_1_out_7, dec4_1_out_8,
       dec4_1_out_9, dec4_1_out_10, dec4_1_out_11, dec4_1_out_12, dec4_1_out_13, dec4_1_out_14,
       dec4_1_out_15, dec4_1_out_16, dec4_1_out_17, dec4_2_out_2, dec4_2_out_3, dec4_2_out_4, dec4_2_out_5,
       dec4_2_out_6, dec4_2_out_7, dec4_2_out_8, dec4_2_out_9, dec4_2_out_10, dec4_2_out_11, dec4_2_out_12,
       dec4_2_out_13, dec4_2_out_14, dec4_2_out_15, dec4_2_out_16, dec4_2_out_17;

  DEC4 dec4_1 (
    .in_1(address[7:4]), .out_2(dec4_1_out_2), .out_3(dec4_1_out_3), .out_4(dec4_1_out_4),
    .out_5(dec4_1_out_5), .out_6(dec4_1_out_6), .out_7(dec4_1_out_7), .out_8(dec4_1_out_8),
    .out_9(dec4_1_out_9), .out_10(dec4_1_out_10), .out_11(dec4_1_out_11), .out_12(dec4_1_out_12),
    .out_13(dec4_1_out_13), .out_14(dec4_1_out_14), .out_15(dec4_1_out_15), .out_16(dec4_1_out_16),
    .out_17(dec4_1_out_17));
  DEC4 dec4_2 (
    .in_1(address[3:0]), .out_2(dec4_2_out_2), .out_3(dec4_2_out_3), .out_4(dec4_2_out_4),
    .out_5(dec4_2_out_5), .out_6(dec4_2_out_6), .out_7(dec4_2_out_7), .out_8(dec4_2_out_8),
    .out_9(dec4_2_out_9), .out_10(dec4_2_out_10), .out_11(dec4_2_out_11), .out_12(dec4_2_out_12),
    .out_13(dec4_2_out_13), .out_14(dec4_2_out_14), .out_15(dec4_2_out_15), .out_16(dec4_2_out_16),
    .out_17(dec4_2_out_17));
endmodule

module RamMemoryDemo (
  input  [7:0] data,
  input  [7:0] address,
  input  set,
  input  emmit,
  output [7:0] emmition,
  output [7:0] memory
);

  wire and_1_out, and_2_out, and_3_out, dec4_1_p2, dec4_2_p2;

  // DEC4 dec4_1: pin names not known; wires that end beside it: address[7:4], dec4_1_p2
  // DEC4 dec4_2: pin names not known; wires that end beside it: address[3:0], dec4_2_p2
  and and_1 (and_1_out, dec4_1_p2, dec4_2_p2);
  and and_2 (and_2_out, and_1_out, set);
  and and_3 (and_3_out, and_1_out, emmit);
  R r_1 (.i(data), .s(and_2_out), .e(and_3_out), .o(emmition), .display(memory));
endmodule

module EightBitmemoryDemo (
  input  [7:0] data,
  input  set,
  output [7:0] out_3
);

  MemoryDemo memorydemo_1 (.InputMemory(data[0]), .SetMemory(set), .memory(out_3[0]));
  MemoryDemo memorydemo_2 (.InputMemory(data[1]), .SetMemory(set), .memory(out_3[1]));
  MemoryDemo memorydemo_3 (.InputMemory(data[2]), .SetMemory(set), .memory(out_3[2]));
  MemoryDemo memorydemo_4 (.InputMemory(data[3]), .SetMemory(set), .memory(out_3[3]));
  MemoryDemo memorydemo_5 (.InputMemory(data[4]), .SetMemory(set), .memory(out_3[4]));
  MemoryDemo memorydemo_6 (.InputMemory(data[5]), .SetMemory(set), .memory(out_3[5]));
  MemoryDemo memorydemo_7 (.InputMemory(data[6]), .SetMemory(set), .memory(out_3[6]));
  MemoryDemo memorydemo_8 (.InputMemory(data[7]), .SetMemory(set), .memory(out_3[7]));
endmodule
